# Fritzing sketch breadboard_components (saved by Fritzing 0.8.7b)
circuit board: 4.8cm x 5.6cm
breadboards: 1

parts:
  J1 = male pin header, 6 pins [form="♂ (male)"]
  J2 = male pin header, 6 pins [form="♂ (male)"]
  Part1 = Breadboard Power Supply Board SMD
  LED2 = LED - 3mm [color="White (4500K)" package="3 mm [THT]"]
  LED3 = LED - 3mm [color="White (4500K)" package="3 mm [THT]"]
  LED4 = LED - 3mm [color="White (4500K)" package="3 mm [THT]"]
  LED5 = LED - 3mm [color="White (4500K)" package="3 mm [THT]"]
  LED6 = LED - 3mm [color="White (4500K)" package="3 mm [THT]"]
  U1 = 74HC595 SMD [package="SO16 [SMD]"]
  part = 74HC595 SMD [package="SO16 [SMD]"]  # not connected
  Q1 = NPN-Transistor [package="TO92 [THT]"]
  R1 = Resistor [tolerance=±5% resistance=100 package="0805 [SMD]"]

nets (from the breadboard view):
  VCC: J1.pin1, Part1.VCC, U1.MR, U1.VCC, R1.Pin_0
  GND: J1.pin6, J2.pin6, Part1.GND, LED2.cathode, LED3.cathode, LED4.cathode, LED5.cathode, LED6.cathode, U1.GND, Q1.E
  N1: J2.pin2, U1.ST_CP
  N2: J2.pin3, U1.SH_CP
  N3: J2.pin4, Q1.B
  N4: J2.pin5, U1.DS
  N5: LED2.anode, U1.Q0
  N6: LED3.anode, U1.Q1
  N7: LED4.anode, U1.Q2
  N8: LED5.anode, U1.Q3
  N9: LED6.anode, U1.Q4
  N10: U1.OE, Q1.C, R1.Pin_1
